// Logisim project Project Generalized SOP Decoder.circ as structural Verilog: 2 circuits, main circuit main
module main (
  input  [2:0] in_1
);

  wire decoder_1_out0, decoder_1_out1, decoder_1_out2, decoder_1_out3, decoder_1_out4, decoder_1_out5,
       decoder_1_out6, decoder_1_out7, or_1_out, or_2_out, or_3_out, or_4_out, or_5_out, or_6_out;

  Decoder #(.select(3)) decoder_1 (
    .out0(decoder_1_out0), .out1(decoder_1_out1), .out2(decoder_1_out2), .out3(decoder_1_out3),
    .out4(decoder_1_out4), .out5(decoder_1_out5), .out6(decoder_1_out6), .out7(decoder_1_out7), .sel(in_1));  // open: en
  or or_1 (or_1_out, decoder_1_out7, decoder_1_out0, decoder_1_out1, decoder_1_out2, decoder_1_out4);
  or or_2 (or_2_out, decoder_1_out7, decoder_1_out6, decoder_1_out1, decoder_1_out3);
  or or_3 (or_3_out, decoder_1_out3, decoder_1_out1, decoder_1_out6, decoder_1_out7, decoder_1_out5, decoder_1_out0, decoder_1_out2);
  or or_4 (or_4_out, decoder_1_out0, decoder_1_out2, decoder_1_out3, decoder_1_out7, decoder_1_out6, decoder_1_out5);
  or or_5 (or_5_out, decoder_1_out3, decoder_1_out1, decoder_1_out5, decoder_1_out6, decoder_1_out7);
  or or_6 (or_6_out, decoder_1_out0, decoder_1_out1, decoder_1_out2, decoder_1_out5, decoder_1_out6, decoder_1_out7);
  _7_Segment_Display u_7_segment_display_1 (
    .g(or_1_out), .f(or_6_out), .a(or_6_out), .b(or_2_out), .e(or_5_out), .d(or_4_out), .c(or_3_out));  // open: dp

  // Notes on the sheet:
  //   D0
  //   D1
  //   D2
  //   D6
  //   D7
  //   D3
  //   D4
  //   D5
  //   Fig. Generalized SOP Decoder
  //   e
  //   c
  //   d
  //   a
  //   f
endmodule

module Generalized_POS_Multiplexer (
);

  wire undriven_28, undriven_29, undriven_30, undriven_58, undriven_59, undriven_60;
  wire [1:0] multiplexer_1_out, multiplexer_2_out, multiplexer_3_out, multiplexer_4_out, multiplexer_5_out,
       multiplexer_6_out, undriven, undriven_2, undriven_3, undriven_4, undriven_5, undriven_6, undriven_7,
       undriven_8, undriven_9, undriven_10, undriven_11, undriven_12, undriven_13, undriven_14, undriven_15,
       undriven_16, undriven_17, undriven_18, undriven_19, undriven_20, undriven_21, undriven_22,
       undriven_23, undriven_24, undriven_31, undriven_32, undriven_33, undriven_34, undriven_35,
       undriven_36, undriven_37, undriven_38, undriven_39, undriven_40, undriven_41, undriven_42,
       undriven_43, undriven_44, undriven_45, undriven_46, undriven_47, undriven_48, undriven_49,
       undriven_50, undriven_51, undriven_52, undriven_53, undriven_54;
  wire [2:0] undriven_25, undriven_26, undriven_27, undriven_55, undriven_56, undriven_57;

  Multiplexer #(.select(3), .width(2)) multiplexer_1 (
    .in0(undriven), .in1(undriven_2), .in2(undriven_3), .in3(undriven_4), .in4(undriven_5), .in5(undriven_6),
    .in6(undriven_7), .in7(undriven_8), .out(multiplexer_1_out), .sel(undriven_25), .en(undriven_28));
  Multiplexer #(.select(3), .width(2)) multiplexer_2 (
    .in0(undriven_9), .in1(undriven_10), .in2(undriven_11), .in3(undriven_12), .in4(undriven_13),
    .in5(undriven_14), .in6(undriven_15), .in7(undriven_16), .out(multiplexer_2_out), .sel(undriven_26),
    .en(undriven_29));
  Multiplexer #(.select(3), .width(2)) multiplexer_3 (
    .in0(undriven_17), .in1(undriven_18), .in2(undriven_19), .in3(undriven_20), .in4(undriven_21),
    .in5(undriven_22), .in6(undriven_23), .in7(undriven_24), .out(multiplexer_3_out), .sel(undriven_27),
    .en(undriven_30));
  Multiplexer #(.select(3), .width(2)) multiplexer_4 (
    .in0(undriven_31), .in1(undriven_32), .in2(undriven_33), .in3(undriven_34), .in4(undriven_35),
    .in5(undriven_36), .in6(undriven_37), .in7(undriven_38), .out(multiplexer_4_out), .sel(undriven_55),
    .en(undriven_58));
  Multiplexer #(.select(3), .width(2)) multiplexer_5 (
    .in0(undriven_39), .in1(undriven_40), .in2(undriven_41), .in3(undriven_42), .in4(undriven_43),
    .in5(undriven_44), .in6(undriven_45), .in7(undriven_46), .out(multiplexer_5_out), .sel(undriven_56),
    .en(undriven_59));
  Multiplexer #(.select(3), .width(2)) multiplexer_6 (
    .in0(undriven_47), .in1(undriven_48), .in2(undriven_49), .in3(undriven_50), .in4(undriven_51),
    .in5(undriven_52), .in6(undriven_53), .in7(undriven_54), .out(multiplexer_6_out), .sel(undriven_57),
    .en(undriven_60));
endmodule
