// Logisim project Project Generalized-SOP-Multiplexer.circ as structural Verilog: 1 circuit, main circuit Generalized POS Multiplexer
module Generalized_POS_Multiplexer (
  input  GND,
  input  [2:0] Inputs
);

  wire multiplexer_1_out, multiplexer_2_out, multiplexer_3_out, multiplexer_4_out, multiplexer_5_out,
       multiplexer_6_out, undriven, undriven_2, undriven_3, undriven_4, undriven_5, undriven_6;

  Multiplexer #(.select(3)) multiplexer_1 (
    .in0(GND), .in1(GND), .in2(GND), .in3(1'b0), .in4(1'b0), .in5(GND), .in6(GND), .in7(GND),
    .out(multiplexer_1_out), .sel(Inputs), .en(undriven));
  Multiplexer #(.select(3)) multiplexer_2 (
    .in0(1'b0), .in1(GND), .in2(1'b0), .in3(GND), .in4(1'b0), .in5(1'b0), .in6(GND), .in7(GND),
    .out(multiplexer_2_out), .sel(Inputs), .en(undriven_2));
  Multiplexer #(.select(3)) multiplexer_3 (
    .in0(GND), .in1(GND), .in2(GND), .in3(GND), .in4(1'b0), .in5(GND), .in6(GND), .in7(GND),
    .out(multiplexer_3_out), .sel(Inputs), .en(undriven_3));
  Multiplexer #(.select(3)) multiplexer_4 (
    .in0(GND), .in1(1'b0), .in2(GND), .in3(GND), .in4(1'b0), .in5(GND), .in6(GND), .in7(GND),
    .out(multiplexer_4_out), .sel(Inputs), .en(undriven_4));
  Multiplexer #(.select(3)) multiplexer_5 (
    .in0(1'b0), .in1(GND), .in2(1'b0), .in3(GND), .in4(1'b0), .in5(GND), .in6(GND), .in7(GND),
    .out(multiplexer_5_out), .sel(Inputs), .en(undriven_5));
  Multiplexer #(.select(3)) multiplexer_6 (
    .in0(GND), .in1(GND), .in2(GND), .in3(1'b0), .in4(GND), .in5(1'b0), .in6(1'b0), .in7(GND),
    .out(multiplexer_6_out), .sel(Inputs), .en(undriven_6));
  _7_Segment_Display u_7_segment_display_1 (
    .g(multiplexer_6_out), .f(multiplexer_1_out), .a(multiplexer_1_out), .b(multiplexer_2_out),
    .e(multiplexer_5_out), .d(multiplexer_4_out), .c(multiplexer_3_out));  // open: dp

  // Notes on the sheet:
  //   a
  //   b
  //   c
  //   d
  //   e
  //   g
  //   Fig. Generalized SOP Multiplexer
  //   f
endmodule
