// Logisim project Project Simplified POS Using NOR Gates .circ as structural Verilog: 1 circuit, main circuit main
module main (
  input  A,
  input  B,
  input  C
);

  wire nor_1_out, nor_2_out, nor_3_out, nor_4_out, nor_5_out, nor_6_out, nor_7_out, nor_8_out, nor_9_out,
       nor_10_out, nor_11_out, nor_12_out, nor_14_out, nor_15_out, nor_16_out, nor_17_out, nor_18_out,
       nor_19_out, nor_20_out, nor_21_out;

  nor nor_1 (nor_1_out, B, B);
  nor nor_2 (nor_2_out, C, C);
  nor nor_3 (nor_3_out, A, A);
  nor nor_4 (nor_4_out, A, C);
  nor nor_5 (nor_5_out, B, C);
  nor nor_6 (nor_6_out, A, A);
  nor nor_7 (nor_7_out, A, A);
  nor nor_8 (nor_8_out, C, C);
  nor nor_9 (nor_9_out, A, A);
  nor nor_10 (nor_10_out, B, C);
  nor nor_11 (nor_11_out, B, B);
  nor nor_12 (nor_12_out, C, C);
  // NOR_Gate nor_13 has open pins: in0=A, in1=A, out=open
  nor nor_14 (nor_14_out, nor_6_out, B);
  nor nor_15 (nor_15_out, A, B, nor_8_out);
  nor nor_16 (nor_16_out, nor_9_out, B, C);
  nor nor_17 (nor_17_out, nor_3_out, B, C);
  nor nor_18 (nor_18_out, A, C);
  nor nor_19 (nor_19_out, A, nor_11_out, nor_12_out);
  nor nor_20 (nor_20_out, A, nor_1_out, nor_2_out);
  nor nor_21 (nor_21_out, nor_7_out, B, C);
  // NOR_Gate nor_22 has open pins: in0=nor_20_out, in1=nor_17_out, out=open
  // NOR_Gate nor_23 has open pins: in0=nor_4_out, in1=nor_5_out, in2=nor_14_out, out=open
  // NOR_Gate nor_24 has open pins: in0=nor_21_out, in1=nor_21_out, out=open
  // NOR_Gate nor_25 has open pins: in0=nor_15_out, in1=nor_16_out, out=open
  // NOR_Gate nor_26 has open pins: in0=nor_18_out, in1=nor_10_out, out=open
  // NOR_Gate nor_27 has open pins: in0=nor_19_out, out=open

  // Notes on the sheet:
  //   (B+C)'
  //   (A'+B)'
  //   (A+B+C')'
  //   (A'+B+C)'
  //   (A+C)'
  //   (A+B'+C')'
  //   (A+B'+C')'
  //   (A'+B+C)'
  //   (A'+B+C)'
  //   a
  //   b
  //   c
  //   d
  //   e
  //   g
endmodule
