// Logisim project Project Simplified POS.circ as structural Verilog: 1 circuit, main circuit main
module main (
  input  in_1,
  input  in_2,
  input  in_3
);

  wire and_1_out, and_2_out, and_3_out, and_4_out, and_5_out, and_6_out, not_1_out, not_2_out, not_3_out,
       or_1_out, or_2_out, or_3_out, or_4_out, or_5_out, or_6_out, or_7_out, or_8_out;

  not not_1 (not_1_out, in_2);
  not not_2 (not_2_out, in_1);
  not not_3 (not_3_out, in_3);
  or or_1 (or_1_out, in_1, not_1_out, not_3_out);
  or or_2 (or_2_out, not_2_out, in_2, in_3);
  or or_3 (or_3_out, in_1, in_3);
  or or_4 (or_4_out, in_2, in_3);
  or or_5 (or_5_out, not_2_out, in_2);
  or or_6 (or_6_out, in_1, in_2, not_3_out);
  or or_7 (or_7_out, not_2_out, in_2, not_3_out);
  or or_8 (or_8_out, not_2_out, not_1_out, in_3);
  and and_1 (and_1_out, or_1_out, or_2_out);
  and and_2 (and_2_out, or_3_out, or_5_out, or_4_out);
  and and_3 (and_3_out, or_2_out, or_2_out);
  and and_4 (and_4_out, or_6_out, or_2_out);
  and and_5 (and_5_out, or_3_out, or_4_out);
  and and_6 (and_6_out, or_1_out, or_7_out, or_8_out);
  _7_Segment_Display u_7_segment_display_1 (
    .g(and_6_out), .f(and_1_out), .a(and_1_out), .b(and_2_out), .e(and_5_out), .d(and_4_out), .c(and_3_out));  // open: dp

  // Notes on the sheet:
  //   A+B'+C'
  //   A'+B+C
  //   A+C
  //   B+C
  //   A'+B
  //   A+B+C'
  //   A'+B+C'
  //   A'+B'+C
  //   simplified pos equation using basic gate
  //   a
  //   b
  //   c
  //   d
  //   e
  //   g
endmodule
