// Logisim project Project Simplified-POS-NOR.circ as structural Verilog: 1 circuit, main circuit main
module main (
  input  A,
  input  B,
  input  C
);

  wire nor_1_out, nor_2_out, nor_3_out, nor_4_out, nor_5_out, nor_6_out, nor_7_out, nor_8_out, nor_9_out,
       nor_10_out, nor_11_out, nor_12_out, nor_13_out, nor_14_out, nor_15_out, nor_16_out, nor_17_out,
       nor_18_out, nor_19_out, nor_20_out, nor_21_out, nor_22_out, nor_23_out, nor_24_out, nor_25_out,
       nor_26_out, nor_27_out, nor_28_out, nor_29_out, nor_30_out, nor_31_out, nor_32_out;

  nor nor_1 (nor_1_out, B, B);
  nor nor_2 (nor_2_out, C, C);
  nor nor_3 (nor_3_out, A, A);
  nor nor_4 (nor_4_out, A, C);
  nor nor_5 (nor_5_out, B, C);
  nor nor_6 (nor_6_out, A, A);
  nor nor_7 (nor_7_out, A, A);
  nor nor_8 (nor_8_out, C, C);
  nor nor_9 (nor_9_out, A, A);
  nor nor_10 (nor_10_out, B, C);
  nor nor_11 (nor_11_out, B, B);
  nor nor_12 (nor_12_out, C, C);
  nor nor_13 (nor_13_out, B, B);
  nor nor_14 (nor_14_out, A, A);
  nor nor_15 (nor_15_out, A, A);
  nor nor_16 (nor_16_out, nor_6_out, B);
  nor nor_17 (nor_17_out, A, B, nor_8_out);
  nor nor_18 (nor_18_out, nor_9_out, B, C);
  nor nor_19 (nor_19_out, nor_13_out, C, nor_14_out);
  nor nor_20 (nor_20_out, C, C);
  nor nor_21 (nor_21_out, nor_3_out, B, C);
  nor nor_22 (nor_22_out, A, C);
  nor nor_23 (nor_23_out, A, nor_11_out, nor_12_out);
  nor nor_24 (nor_24_out, B, nor_15_out, nor_20_out);
  nor nor_25 (nor_25_out, A, nor_1_out, nor_2_out);
  nor nor_26 (nor_26_out, nor_7_out, B, C);
  nor nor_27 (nor_27_out, nor_25_out, nor_21_out);
  nor nor_28 (nor_28_out, nor_4_out, nor_5_out, nor_16_out);
  nor nor_29 (nor_29_out, nor_26_out, nor_26_out);
  nor nor_30 (nor_30_out, nor_17_out, nor_18_out);
  nor nor_31 (nor_31_out, nor_22_out, nor_10_out);
  nor nor_32 (nor_32_out, nor_23_out, nor_19_out, nor_24_out);
  _7_Segment_Display u_7_segment_display_1 (
    .g(nor_32_out), .f(nor_27_out), .a(nor_27_out), .b(nor_28_out), .e(nor_31_out), .d(nor_30_out),
    .c(nor_29_out));  // open: dp

  // Notes on the sheet:
  //   (B+C)'
  //   (A'+B)'
  //   (A+B+C')'
  //   (A'+B+C)'
  //   (A+C)'
  //   (A+B'+C')'
  //   (A+B'+C')'
  //   (A'+B+C)'
  //   (A'+B+C)'
  //   Figure: Simplified POS using NOR gate
  //   a
  //   b
  //   c
  //   d
  //   e
  //   g
  //   f
endmodule
