// Logisim project Project-Sequential Circuit.circ as structural Verilog: 1 circuit, main circuit Generalized SOP Using Decoder,AND gate, OR Gates
module Generalized_SOP_Using_Decoder_AND_gate__OR_Gates (
);

  wire and_1_out, clock_1_out, decoder_1_out0, decoder_1_out1, decoder_1_out2, decoder_1_out3,
       decoder_1_out4, decoder_1_out5, decoder_1_out6, decoder_1_out7, or_1_out, or_2_out, or_3_out,
       or_4_out, or_5_out, or_6_out;
  wire [2:0] t_ff_1_q;

  Clock clock_1 (.out(clock_1_out));
  T_Flip_Flop t_ff_1 (.clk(clock_1_out), .T(1'b1), .Q(t_ff_1_q[0]));  // open: Qn, preset, reset, en
  T_Flip_Flop t_ff_2 (.clk(clock_1_out), .T(t_ff_1_q[0]), .Q(t_ff_1_q[1]));  // open: Qn, preset, reset, en
  T_Flip_Flop t_ff_3 (.clk(clock_1_out), .T(and_1_out), .Q(t_ff_1_q[2]));  // open: Qn, preset, reset, en
  and and_1 (and_1_out, t_ff_1_q[1], t_ff_1_q[0]);
  Decoder #(.select(3)) decoder_1 (
    .out0(decoder_1_out0), .out1(decoder_1_out1), .out2(decoder_1_out2), .out3(decoder_1_out3),
    .out4(decoder_1_out4), .out5(decoder_1_out5), .out6(decoder_1_out6), .out7(decoder_1_out7),
    .sel(t_ff_1_q), .en(1'b1));
  or or_1 (or_1_out, decoder_1_out7, decoder_1_out0, decoder_1_out1, decoder_1_out2, decoder_1_out4);
  or or_2 (or_2_out, decoder_1_out7, decoder_1_out6, decoder_1_out1, decoder_1_out3);
  or or_3 (or_3_out, decoder_1_out3, decoder_1_out1, decoder_1_out6, decoder_1_out7, decoder_1_out5, decoder_1_out0, decoder_1_out2);
  or or_4 (or_4_out, decoder_1_out0, decoder_1_out2, decoder_1_out3, decoder_1_out7, decoder_1_out6, decoder_1_out5);
  or or_5 (or_5_out, decoder_1_out3, decoder_1_out1, decoder_1_out5, decoder_1_out6, decoder_1_out7);
  or or_6 (or_6_out, decoder_1_out0, decoder_1_out1, decoder_1_out2, decoder_1_out5, decoder_1_out6, decoder_1_out7);
  _7_Segment_Display u_7_segment_display_1 (
    .g(or_1_out), .f(or_6_out), .a(or_6_out), .b(or_2_out), .e(or_5_out), .d(or_4_out), .c(or_3_out));  // open: dp

  // Notes on the sheet:
  //   T-C
  //   T-B
  //   T-A
  //   MEMORY-3bit Synchronus Counter Using  (T-Flip-Flop)
  //   D0
  //   D1
  //   D2
  //   D5
  //   D6
  //   D7
  //   Fig. Generalized SOP Sequential Circuit Using Decoder,AND gate,OR gates,T-flip-flops
  //   D3
  //   D4
  //   d
  //   e
  //   g
  //   a
  //   b
  //   f
  //   c
endmodule
