// Logisim project Project-Simplifeid-SOP.circ as structural Verilog: 1 circuit, main circuit Project-Simplified SOP Circuit Diagram Using Basic Gates
module Project_Simplified_SOP_Circuit_Diagram_Using_Basic_Gates (
  input  A,
  input  B,
  input  C
);

  wire and_1_out, and_2_out, and_3_out, and_4_out, and_5_out, and_6_out, and_7_out, and_8_out, and_9_out,
       not_1_out, not_2_out, not_3_out, or_1_out, or_2_out, or_3_out, or_4_out, or_5_out, or_6_out;

  not not_1 (not_1_out, A);
  not not_2 (not_2_out, B);
  not not_3 (not_3_out, C);
  and and_1 (and_1_out, not_1_out, not_2_out);
  and and_2 (and_2_out, not_2_out, C);
  and and_3 (and_3_out, A, C);
  and and_4 (and_4_out, A, B);
  and and_5 (and_5_out, B, not_3_out);
  and and_6 (and_6_out, not_1_out, C);
  and and_7 (and_7_out, not_1_out, not_3_out);
  and and_8 (and_8_out, not_2_out, not_3_out);
  and and_9 (and_9_out, A, B, C);
  or or_1 (or_1_out, and_1_out, and_2_out, and_3_out, and_4_out, and_5_out);
  or or_2 (or_2_out, and_4_out, and_6_out);
  or or_3 (or_3_out, and_1_out, B, C, and_7_out);
  or or_4 (or_4_out, and_7_out, B, and_3_out);
  or or_5 (or_5_out, and_4_out, C);
  or or_6 (or_6_out, and_1_out, and_8_out, and_7_out, and_9_out);
  _7_Segment_Display u_7_segment_display_1 (
    .g(or_6_out), .f(or_1_out), .a(or_1_out), .b(or_2_out), .e(or_5_out), .d(or_4_out), .c(or_3_out));  // open: dp

  // Notes on the sheet:
  //   Fig. Project-Simplifeid SOP Circuit Diagram using basic gates
  //   b
  //   c
  //   e
  //   a
  //   d
  //   g
  //   f
endmodule
