// Logisim project Project-Simplified SOP Using NAND.circ as structural Verilog: 1 circuit, main circuit main
module main (
  input  A,
  input  B,
  input  C
);

  wire nand_1_out, nand_2_out, nand_3_out, nand_4_out, nand_5_out, nand_6_out, nand_7_out, nand_8_out,
       nand_9_out, nand_10_out, nand_11_out, nand_12_out, nand_13_out, nand_14_out, nand_15_out, nand_16_out,
       nand_17_out, nand_18_out, nand_19_out, nand_20_out, nand_21_out, nand_22_out, nand_23_out,
       nand_24_out, nand_25_out, nand_26_out, nand_27_out, nand_28_out, nand_29_out, nand_30_out, undriven;

  nand nand_1 (nand_1_out, A, A);
  nand nand_2 (nand_2_out, B, B);
  nand nand_3 (nand_3_out, A, C);
  nand nand_4 (nand_4_out, A, B);
  nand nand_5 (nand_5_out, C, C);
  nand nand_6 (nand_6_out, A, A);
  nand nand_7 (nand_7_out, A, B);
  nand nand_8 (nand_8_out, A, A);
  nand nand_9 (nand_9_out, B, B);
  nand nand_10 (nand_10_out, C, C);
  nand nand_11 (nand_11_out, A, C);
  nand nand_12 (nand_12_out, A, B);
  nand nand_13 (nand_13_out, C, C);
  nand nand_14 (nand_14_out, B, B);
  nand nand_15 (nand_15_out, C, C);
  nand nand_16 (nand_16_out, A, B, C);
  nand nand_17 (nand_17_out, nand_1_out, nand_2_out);
  nand nand_18 (nand_18_out, nand_5_out, B);
  nand nand_19 (nand_19_out, nand_6_out, C);
  nand nand_20 (nand_20_out, C, C);
  nand nand_21 (nand_21_out, nand_14_out, nand_15_out);
  nand nand_22 (nand_22_out, nand_2_out, C);
  nand nand_23 (nand_23_out, nand_8_out, nand_9_out);
  nand nand_24 (nand_24_out, nand_8_out, nand_10_out);
  nand nand_25 (nand_25_out, nand_12_out, nand_13_out);
  nand nand_26 (nand_26_out, nand_19_out, nand_7_out);
  nand nand_27 (nand_27_out, nand_24_out, nand_11_out, nand_9_out);
  nand nand_28 (nand_28_out, nand_23_out, nand_24_out, nand_20_out, nand_9_out);
  nand nand_29 (nand_29_out, nand_17_out, nand_22_out, nand_3_out, nand_4_out, nand_18_out);
  nand nand_30 (nand_30_out, nand_17_out, nand_21_out, nand_24_out, nand_16_out);
  _7_Segment_Display u_7_segment_display_1 (
    .g(nand_30_out), .f(nand_29_out), .a(nand_29_out), .b(nand_26_out), .e(nand_25_out), .d(nand_27_out),
    .c(nand_28_out), .dp(undriven));

  // Notes on the sheet:
  //   A'
  //   B'
  //   A'+C'
  //   A'+B'
  //   C'
  //   A'+B'
  //   A'
  //   B'
  //   C'
  //   A'+C'
  //   B'
  //   C'
  //   A+B
  //   B'+C
  //   A+C'
  //   C'
  //   B+C
  //   A'B'
  //   B+C'
  //   A+B
  //   A+C
  //   e
  //   b
  //   d
  //   A'C'+AC+
  //   B
  //   B'C'
  //   Fig.  Circuit Diagram of SOP using only NAND Gates
  //   c
  //   a
  //   AB
  //   A'C+
  //          A'B'+A'C'+B+C
  //   g
endmodule
